# Fritzing sketch PiPower HAT (saved by Fritzing 0.9.3b)
circuit board: 6.52541cm x 5.62539cm
breadboards: 1

parts:
  JACK2 = 2.1mm DC Barrel Jack
  JACK1 = USB_AB [package=usb-ab-micro-smd]
  J1 = Cobbler Plus Cable
  Button = male pin header, 4 pins [form="♂ (male)"]
  Q1 = Basic FET N-Channel [package="DPak [SMD]"]
  Arduino = Arduino Pro Mini (5V)

nets:
  N1: JACK2.center, JACK1.VBUS, Arduino.RAW
  GND: JACK2.sleeve, JACK1.GND, J1.GND#8, J1.GND#24, J1.GND#38, Button.pin2, Button.pin3, Arduino.GND
  N2: J1.5.0V#1, Q1.drain
  N3: J1.TXD, Arduino.RXI
  N4: J1.RXD, Arduino.TXO
  N5: Button.pin1, Arduino.SCK
  N6: Button.pin4, Arduino.D3
  N7: Q1.Gate, Arduino.D9
  N8: Q1.source, Arduino.VCC

custom parts:
  2.1mm DC Barrel Jack: 2.1mm DC Barrel Jack with Thru-Hole Connectors (breadboardable)
  Cobbler Plus Cable: The Cobbler Plus is an add on prototyping board from Adafruit specifically designed for the Raspberry Pi B+ that can break out all those tasty power, GPIO, I2C and SPI pins from the 40-pin header onto a solderless breadboard. This set will make "cobbling together" prototypes with the Pi super easy. The Cobbler Plus can plug into any solderless breadboard.
